# Fritzing sketch finalprojectschematic (saved by Fritzing 0.9.3b)
breadboards: 1

parts:
  LCD1 = LCD screen
  Part3 = Arduino Uno (Rev3)
  R2 = Resistor [tolerance=±5% resistance=220 package="2010 [SMD]"]
  R3 = Resistor [tolerance=±5% resistance=220 package="0805 [SMD]"]
  Part4 = Real Time Clock Module - DS1307 RTC Breakout Board

nets:
  GND: LCD1.VSS, LCD1.R/W, LCD1.LED-, Part3.GND, R2.Pin_0, Part4.GND
  5V: LCD1.VDD, Part3.5V, R3.Pin_0, Part4.5V
  N1: LCD1.V0, R2.Pin_1
  N2: LCD1.RS, Part3.D12/MISO
  N3: LCD1.E, Part3.D11_PWM/MOSI
  N4: LCD1.DB4, Part3.D5_PWM
  N5: LCD1.DB5, Part3.D4
  N6: LCD1.DB6, Part3.D3_PWM
  N7: LCD1.DB7, Part3.D2
  N8: LCD1.LED+, R3.Pin_1
  N9: Part3.A4/SDA, Part4.SDA
  N10: Part3.A5/SCL, Part4.SCL
